# Fritzing sketch Laser Image Projecter (saved by Fritzing 0.9.1b)
breadboards: 2

parts:
  M1 = DC Motor
  Part1 = Arduino Uno (Rev3) - ICSP
  U1 = 74HC595 [package="DIP16 [THT]"]
  U2 = 74HC595 [package="DIP16 [THT]"]
  Q1 = PNP-Transistor [package="TO92 [THT]"]
  VCC1 = 4 x AAA Battery Mount
  LD15 = LD
  R1 = Resistor [package="2512 [SMD]"]
  LD5 = LD
  LD13 = LD
  LD1 = LD
  LD6 = LD
  LD8 = LD
  LD2 = LD
  LD3 = LD
  LD14 = LD
  LD10 = LD
  LD7 = LD
  LD9 = LD
  LD4 = LD
  LD12 = LD
  LD16 = LD
  LD11 = LD

nets:
  N1: M1.pin_1, Q1.E
  N2: M1.pin_2, VCC1.+
  N3: Part1.ICSP_MOSI, Part1.D11_PWM/MOSI, U2.DS
  N4: Part1.D8, U1.ST_CP, U2.ST_CP
  N5: Part1.D12/MISO, U1.SH_CP, U2.Q7', U2.SH_CP
  GND: Part1.GND, U1.GND, U1.OE, U2.GND, U2.OE, LD15.cathode, LD5.cathode, LD13.cathode, LD1.cathode, LD6.cathode, LD8.cathode, LD2.cathode, LD3.cathode, LD14.cathode, LD10.cathode, LD7.cathode, LD9.cathode, LD4.cathode, LD12.cathode, LD16.cathode, LD11.cathode
  N6: Part1.D3_PWM, R1.Pin_0
  VCC: Part1.5V, U1.MR, U1.VCC, U2.MR, U2.VCC
  N7: U1.Q1, LD11.anode
  N8: U1.Q2, LD10.anode
  N9: U1.Q3, LD12.anode
  N10: U1.Q4, LD14.anode
  N11: U1.Q5, LD16.anode
  N12: U1.Q6, LD13.anode
  N13: U1.Q7, LD15.anode
  N14: U1.Q0, LD9.anode
  N15: U2.Q1, LD2.anode
  N16: U2.Q2, LD3.anode
  N17: U2.Q3, LD4.anode
  N18: U2.Q4, LD5.anode
  N19: U2.Q5, LD8.anode
  N20: U2.Q6, LD6.anode
  N21: U2.Q7, LD7.anode
  N22: U2.Q0, LD1.anode
  N23: Q1.B, R1.Pin_1
  N24: Q1.C, VCC1.-

custom parts:
  LD: A Generic Red Dot Laser Diode Module (~5mW)
